// Logisim project CSC220_Project_Test1 copy.circ as structural Verilog: 1 circuit, main circuit m
module m (
  input  [3:0] S3S2S1S0,
  input  [7:0] X,
  input  [7:0] Y,
  output V,
  output C,
  output [7:0] G,
  output Z,
  output N
);

  wire and_1_out, and_2_out;
  wire [0:0] not_2_out;
  wire [7:0] adder_1_out, multiplexer_1_out, multiplexer_2_out, nand_1_out, not_1_out, not_3_out, not_4_out,
       or_1_out, xor_1_out;

  assign not_1_out = ~Y;  // NOT_Gate not_1, 8 bits wide
  not not_2 (not_2_out[0], Y[7]);
  Multiplexer #(.select(2), .width(8)) multiplexer_1 (
    .in0(not_1_out), .in1({8{1'b0}}), .in2(8'h2), .in3(X), .out(multiplexer_1_out), .sel(S3S2S1S0[2:1]));  // open: en
  assign not_3_out = ~X;  // NOT_Gate not_3, 8 bits wide
  assign not_4_out = ~Y;  // NOT_Gate not_4, 8 bits wide
  Adder adder_1 (.a(X), .b(multiplexer_1_out), .out(adder_1_out), .cin(S3S2S1S0[0]), .cout(C));
  assign xor_1_out = X ^ Y;  // XOR_Gate xor_1, 8 bits wide
  assign or_1_out = X | not_4_out;  // OR_Gate or_1, 8 bits wide
  assign nand_1_out = ~(X & Y);  // NAND_Gate nand_1, 8 bits wide
  Multiplexer #(.select(3), .width(8), .enable("false")) multiplexer_2 (
    .in0(xor_1_out), .in1(or_1_out), .in2(nand_1_out), .in3(not_3_out), .in4(Y), .in5({{2{Y[7]}}, Y[6:1]}),
    .in6({1'b0, Y[7:1]}), .in7({Y[6:0], not_2_out[0]}), .out(multiplexer_2_out), .sel(S3S2S1S0[2:0]));
  Multiplexer #(.width(8), .enable("false")) multiplexer_3 (
    .in0(adder_1_out), .in1(multiplexer_2_out), .out(G), .sel(S3S2S1S0[3]));
  and and_1 (and_1_out, ~adder_1_out[7], X[7], multiplexer_1_out[7]);  // AND_Gate
  and and_2 (and_2_out, adder_1_out[7], ~X[7], ~multiplexer_1_out[7]);  // AND_Gate
  or or_2 (V, and_1_out, and_2_out);
  nor nor_1 (Z, G[0], G[1], G[2], G[3], G[4], G[5], G[6], G[7]);

  assign N = G[7];
endmodule
